# Fritzing sketch ricecooker (saved by Fritzing 0.9.2b)
breadboards: 1

parts:
  Part1 = Arduino Uno (Rev3)
  LCD1 = LCD screen
  R1 = Trimmer Potentiometer [maximum_resistance=10kΩ package=THT]
  R2 = Resistor [tolerance=±5% resistance=220 package=THT]
  U1 = 2-Channel 5v Relay Shield [package=relay-2ch5v10a]
  LED1 = LED - 5mm [color="Yellow (592nm)" package="5 mm [THT]"]
  LED2 = LED - 5mm [color="Yellow (595nm)" package="5 mm [THT]"]
  LED3 = LED - 5mm [color="Green (570nm)" package="5 mm [THT]"]
  LED4 = LED - 5mm [color="Red (633nm)" package="5 mm [THT]"]
  LED5 = LED - 5mm [color="Orange (620nm)" package="5 mm [THT]"]
  S2 = Pushbutton [package=THT]
  S3 = Pushbutton [package=THT]
  S4 = Pushbutton [package=THT]
  S5 = Pushbutton [package=THT]
  S6 = Pushbutton [package=THT]

nets:
  N1: Part1.A5/SCL, U1.IN2
  GND: Part1.D8, Part1.D9_PWM, Part1.D13/SCK, Part1.GND, Part1.D6_PWM, Part1.D7, LCD1.VSS, LCD1.R/W, LCD1.LED-, R1.leg1, U1.GND, LED1.cathode, LED2.cathode, LED3.cathode, LED4.cathode, LED5.cathode
  N2: Part1.D10_PWM/SS, U1.IN1
  N3: Part1.D11_PWM/MOSI, LCD1.E
  N4: Part1.D12/MISO, LCD1.RS
  N5: Part1.D2, LCD1.DB7
  N6: Part1.D3_PWM, LCD1.DB6
  N7: Part1.D4, LCD1.DB5
  N8: Part1.D5_PWM, LCD1.DB4
  5V: Part1.5V, LCD1.VDD, R1.leg2, R2.Pin_0, U1.VCC, S2.leg0, S3.leg0, S4.leg0, S5.leg0, S6.leg0
  N9: LCD1.V0, R1.wiper
  N10: LCD1.LED+, R2.Pin_1

custom parts:
  2-Channel 5v Relay Shield: 2 Channel 5v Relay Shield w. 2x SPD-06VDC-SD-C
